// Logisim project dflipflopen.circ as structural Verilog: 7 circuits, main circuit D Flip-flop w/ enable
module D_Flip_flop_w__enable (
  input  WD,
  input  D,
  input  CLK,
  output Q,
  output QN
);

  wire pull_resistor_1_node, pull_resistor_2_node, pull_resistor_3_node, pull_resistor_4_node,
       pull_resistor_5_node, pull_resistor_6_node, pull_resistor_7_node, transistor_3_out, transistor_5_out,
       transistor_7_out, transistor_9_out, transistor_11_out, transistor_14_out, transistor_16_out;

  Pull_Resistor #(.pull(1)) pull_resistor_1 (.node(pull_resistor_1_node));
  Transistor #(.\type ("n")) transistor_1 (.in(1'b0), .out(pull_resistor_1_node), .gate(WD));
  Pull_Resistor #(.pull(1)) pull_resistor_2 (.node(pull_resistor_2_node));
  Transistor #(.\type ("n")) transistor_2 (.in(transistor_3_out), .out(pull_resistor_2_node), .gate(WD));
  Transistor #(.\type ("n")) transistor_3 (.in(1'b0), .out(transistor_3_out), .gate(D));
  Pull_Resistor #(.pull(1)) pull_resistor_3 (.node(pull_resistor_3_node));
  Transistor #(.\type ("n")) transistor_4 (.in(transistor_5_out), .out(pull_resistor_3_node), .gate(Q));
  Transistor #(.\type ("n")) transistor_5 (.in(1'b0), .out(transistor_5_out), .gate(pull_resistor_1_node));
  Pull_Resistor #(.pull(1)) pull_resistor_4 (.node(pull_resistor_4_node));
  Transistor #(.\type ("n")) transistor_6 (
    .in(transistor_7_out), .out(pull_resistor_4_node), .gate(pull_resistor_3_node));
  Transistor #(.\type ("n")) transistor_7 (.in(1'b0), .out(transistor_7_out), .gate(pull_resistor_2_node));
  Pull_Resistor #(.pull(1)) pull_resistor_5 (.node(pull_resistor_5_node));
  Transistor #(.\type ("n")) transistor_8 (
    .in(transistor_9_out), .out(pull_resistor_5_node), .gate(pull_resistor_4_node));
  Transistor #(.\type ("n")) transistor_9 (.in(1'b0), .out(transistor_9_out), .gate(CLK));
  Pull_Resistor #(.pull(1)) pull_resistor_6 (.node(pull_resistor_6_node));
  Transistor #(.\type ("n")) transistor_10 (.in(transistor_11_out), .out(pull_resistor_6_node), .gate(CLK));
  Transistor #(.\type ("n")) transistor_11 (.in(1'b0), .out(transistor_11_out), .gate(pull_resistor_7_node));
  Pull_Resistor #(.pull(1)) pull_resistor_7 (.node(pull_resistor_7_node));
  Transistor #(.\type ("n")) transistor_12 (.in(1'b0), .out(pull_resistor_7_node), .gate(pull_resistor_4_node));
  Pull_Resistor #(.pull(1)) pull_resistor_8 (.node(Q));
  Transistor #(.\type ("n")) transistor_13 (.in(transistor_14_out), .out(Q), .gate(pull_resistor_5_node));
  Transistor #(.\type ("n")) transistor_14 (.in(1'b0), .out(transistor_14_out), .gate(QN));
  Pull_Resistor #(.pull(1)) pull_resistor_9 (.node(QN));
  Transistor #(.\type ("n")) transistor_15 (.in(transistor_16_out), .out(QN), .gate(Q));
  Transistor #(.\type ("n")) transistor_16 (.in(1'b0), .out(transistor_16_out), .gate(pull_resistor_6_node));
endmodule

module _2x1_Mux (
  input  A,
  input  B,
  input  S0,
  output Y
);

  wire pull_resistor_1_node, pull_resistor_2_node, pull_resistor_3_node, transistor_3_out, transistor_5_out,
       transistor_7_out;

  Pull_Resistor #(.pull(1)) pull_resistor_1 (.node(pull_resistor_1_node));
  Transistor #(.\type ("n")) transistor_1 (.in(1'b0), .out(pull_resistor_1_node), .gate(S0));
  Pull_Resistor #(.pull(1)) pull_resistor_2 (.node(pull_resistor_2_node));
  Transistor #(.\type ("n")) transistor_2 (.in(transistor_3_out), .out(pull_resistor_2_node), .gate(A));
  Transistor #(.\type ("n")) transistor_3 (.in(1'b0), .out(transistor_3_out), .gate(pull_resistor_1_node));
  Pull_Resistor #(.pull(1)) pull_resistor_3 (.node(pull_resistor_3_node));
  Transistor #(.\type ("n")) transistor_4 (.in(transistor_5_out), .out(pull_resistor_3_node), .gate(S0));
  Transistor #(.\type ("n")) transistor_5 (.in(1'b0), .out(transistor_5_out), .gate(B));
  Pull_Resistor #(.pull(1)) pull_resistor_4 (.node(Y));
  Transistor #(.\type ("n")) transistor_6 (.in(transistor_7_out), .out(Y), .gate(pull_resistor_2_node));
  Transistor #(.\type ("n")) transistor_7 (.in(1'b0), .out(transistor_7_out), .gate(pull_resistor_3_node));
endmodule

module tests (
  input  in_1,
  input  in_2,
  input  in_3,
  input  in_4,
  input  WD,
  input  WD_2,
  input  D,
  input  D_2,
  input  CLK,
  output out_10,
  output out_11,
  output Q,
  output Q_2,
  output QN,
  output QN_2
);

  wire clock_1_out, clock_2_out, clock_3_out, nand_1_out, nand_2_out, nand_3_out, nand_4_out, nand_7_out,
       not_1_out, not_2_out, pull_resistor_1_node, pull_resistor_3_node, pull_resistor_4_node,
       pull_resistor_7_node, pull_resistor_8_node, pull_resistor_9_node, pull_resistor_11_node,
       pull_resistor_13_node, pull_resistor_14_node, pull_resistor_15_node, pull_resistor_20_node,
       pull_resistor_23_node, pull_resistor_24_node, transistor_2_out, transistor_3_out, transistor_4_out,
       transistor_7_out, transistor_8_out, transistor_9_out, transistor_10_out, transistor_12_out,
       transistor_14_out, transistor_16_out, transistor_17_out, transistor_19_out, transistor_21_out,
       transistor_23_out, transistor_25_out, transistor_27_out, transistor_29_out, transistor_31_out,
       transistor_33_out, transistor_34_out, transistor_36_out, transistor_37_out, transistor_38_out,
       transistor_39_out, transistor_40_out, transistor_42_out, transistor_43_out, transistor_45_out,
       transistor_48_out;

  Pull_Resistor #(.pull(1)) pull_resistor_1 (.node(pull_resistor_1_node));
  Transistor #(.\type ("n"), .gate("br")) transistor_1 (.in(transistor_3_out), .out(pull_resistor_1_node), .gate(in_2));
  Transistor #(.\type ("n")) transistor_2 (.in(1'b0), .out(transistor_2_out), .gate(transistor_8_out));
  Pull_Resistor #(.pull(1)) pull_resistor_2 (.node(transistor_2_out));
  Transistor #(.\type ("n"), .gate("br")) transistor_3 (.in(1'b0), .out(transistor_3_out), .gate(in_1));
  Transistor #(.\type ("n")) transistor_4 (.in(1'b0), .out(transistor_4_out), .gate(transistor_2_out));
  Pull_Resistor #(.pull(1)) pull_resistor_3 (.node(pull_resistor_3_node));
  Transistor #(.\type ("n")) transistor_5 (.in(1'b0), .out(pull_resistor_3_node), .gate(WD));
  Pull_Resistor #(.pull(1)) pull_resistor_4 (.node(pull_resistor_4_node));
  Transistor #(.\type ("n")) transistor_6 (.in(transistor_7_out), .out(pull_resistor_4_node), .gate(WD));
  Transistor #(.\type ("n")) transistor_7 (.in(1'b0), .out(transistor_7_out), .gate(D_2));
  Clock clock_1 (.out(clock_1_out));
  Transistor #(.\type ("n"), .gate("br")) transistor_8 (
    .in(transistor_9_out), .out(transistor_8_out), .gate(pull_resistor_1_node));
  Pull_Resistor #(.pull(1)) pull_resistor_5 (.node(transistor_8_out));
  Transistor #(.\type ("n"), .gate("br")) transistor_9 (.in(1'b0), .out(transistor_9_out), .gate(pull_resistor_9_node));
  Transistor #(.\type ("n")) transistor_10 (.in(transistor_4_out), .out(transistor_10_out), .gate(clock_2_out));
  Pull_Resistor #(.pull(1)) pull_resistor_6 (.node(transistor_10_out));
  Pull_Resistor #(.pull(1)) pull_resistor_7 (.node(pull_resistor_7_node));
  Transistor #(.\type ("n")) transistor_11 (.in(transistor_12_out), .out(pull_resistor_7_node), .gate(Q));
  Transistor #(.\type ("n")) transistor_12 (.in(1'b0), .out(transistor_12_out), .gate(pull_resistor_3_node));
  Pull_Resistor #(.pull(1)) pull_resistor_8 (.node(pull_resistor_8_node));
  Transistor #(.\type ("n")) transistor_13 (
    .in(transistor_14_out), .out(pull_resistor_8_node), .gate(pull_resistor_7_node));
  Transistor #(.\type ("n")) transistor_14 (.in(1'b0), .out(transistor_14_out), .gate(pull_resistor_4_node));
  Pull_Resistor #(.pull(1)) pull_resistor_9 (.node(pull_resistor_9_node));
  Transistor #(.\type ("n"), .gate("br")) transistor_15 (
    .in(transistor_19_out), .out(pull_resistor_9_node), .gate(out_10));
  Transistor #(.\type ("n")) transistor_16 (.in(transistor_17_out), .out(transistor_16_out), .gate(clock_2_out));
  Pull_Resistor #(.pull(1)) pull_resistor_10 (.node(transistor_16_out));
  Transistor #(.\type ("n")) transistor_17 (.in(1'b0), .out(transistor_17_out), .gate(transistor_8_out));
  Pull_Resistor #(.pull(1)) pull_resistor_11 (.node(pull_resistor_11_node));
  Transistor #(.\type ("n")) transistor_18 (.in(1'b0), .out(pull_resistor_11_node), .gate(pull_resistor_8_node));
  Transistor #(.\type ("n"), .gate("br")) transistor_19 (
    .in(1'b0), .out(transistor_19_out), .gate(pull_resistor_15_node));
  Transistor #(.\type ("n")) transistor_20 (.in(transistor_21_out), .out(transistor_16_out), .gate(out_10));
  Pull_Resistor #(.pull(1)) pull_resistor_12 (.node(transistor_16_out));
  Transistor #(.\type ("n")) transistor_21 (.in(1'b0), .out(transistor_21_out), .gate(transistor_10_out));
  Pull_Resistor #(.pull(1)) pull_resistor_13 (.node(pull_resistor_13_node));
  Transistor #(.\type ("n")) transistor_22 (
    .in(transistor_23_out), .out(pull_resistor_13_node), .gate(pull_resistor_8_node));
  Transistor #(.\type ("n")) transistor_23 (.in(1'b0), .out(transistor_23_out), .gate(clock_1_out));
  Pull_Resistor #(.pull(1)) pull_resistor_14 (.node(pull_resistor_14_node));
  Transistor #(.\type ("n")) transistor_24 (.in(transistor_25_out), .out(pull_resistor_14_node), .gate(clock_1_out));
  Transistor #(.\type ("n")) transistor_25 (.in(1'b0), .out(transistor_25_out), .gate(pull_resistor_11_node));
  Pull_Resistor #(.pull(1)) pull_resistor_15 (.node(pull_resistor_15_node));
  Transistor #(.\type ("n"), .gate("br")) transistor_26 (.in(1'b0), .out(pull_resistor_15_node), .gate(in_2));
  Transistor #(.\type ("n")) transistor_27 (.in(1'b0), .out(transistor_27_out), .gate(transistor_16_out));
  Pull_Resistor #(.pull(1)) pull_resistor_16 (.node(Q));
  Transistor #(.\type ("n")) transistor_28 (.in(transistor_29_out), .out(Q), .gate(pull_resistor_13_node));
  Transistor #(.\type ("n")) transistor_29 (.in(1'b0), .out(transistor_29_out), .gate(QN));
  Pull_Resistor #(.pull(1)) pull_resistor_17 (.node(QN));
  Transistor #(.\type ("n")) transistor_30 (.in(transistor_31_out), .out(QN), .gate(Q));
  Transistor #(.\type ("n")) transistor_31 (.in(1'b0), .out(transistor_31_out), .gate(pull_resistor_14_node));
  Clock clock_2 (.out(clock_2_out));
  Pull_Resistor #(.pull(1)) pull_resistor_18 (.node(out_10));
  Transistor #(.\type ("n")) transistor_32 (.in(transistor_27_out), .out(out_10), .gate(transistor_16_out));
  Transistor #(.\type ("n"), .gate("br")) transistor_33 (.in(transistor_34_out), .out(transistor_33_out), .gate(in_4));
  Pull_Resistor #(.pull(1)) pull_resistor_19 (.node(transistor_33_out));
  Transistor #(.\type ("n"), .gate("br")) transistor_34 (.in(1'b0), .out(transistor_34_out), .gate(in_3));
  Pull_Resistor #(.pull(1)) pull_resistor_20 (.node(pull_resistor_20_node));
  Transistor #(.\type ("n")) transistor_35 (.in(1'b0), .out(pull_resistor_20_node), .gate(transistor_36_out));
  not not_1 (not_1_out, WD_2);
  Transistor #(.\type ("n"), .gate("br")) transistor_36 (
    .in(transistor_39_out), .out(transistor_36_out), .gate(transistor_33_out));
  Pull_Resistor #(.pull(1)) pull_resistor_21 (.node(transistor_36_out));
  Transistor #(.\type ("n")) transistor_37 (.in(transistor_38_out), .out(transistor_37_out), .gate(clock_3_out));
  Transistor #(.\type ("n")) transistor_38 (.in(1'b0), .out(transistor_38_out), .gate(pull_resistor_20_node));
  Pull_Resistor #(.pull(1)) pull_resistor_22 (.node(transistor_37_out));
  nand nand_1 (nand_1_out, Q_2, not_1_out);
  nand nand_2 (nand_2_out, WD_2, D);
  Transistor #(.\type ("n"), .gate("br")) transistor_39 (
    .in(1'b0), .out(transistor_39_out), .gate(pull_resistor_23_node));
  Transistor #(.\type ("n")) transistor_40 (.in(1'b0), .out(transistor_40_out), .gate(transistor_36_out));
  nand nand_3 (nand_3_out, nand_1_out, nand_2_out);
  Pull_Resistor #(.pull(1)) pull_resistor_23 (.node(pull_resistor_23_node));
  Transistor #(.\type ("n"), .gate("br")) transistor_41 (
    .in(transistor_42_out), .out(pull_resistor_23_node), .gate(out_11));
  Transistor #(.\type ("n"), .gate("br")) transistor_42 (.in(1'b0), .out(transistor_42_out), .gate(transistor_45_out));
  Pull_Resistor #(.pull(1)) pull_resistor_24 (.node(pull_resistor_24_node));
  Transistor #(.\type ("n")) transistor_43 (.in(1'b0), .out(transistor_43_out), .gate(transistor_37_out));
  Transistor #(.\type ("n")) transistor_44 (.in(transistor_40_out), .out(pull_resistor_24_node), .gate(clock_3_out));
  not not_2 (not_2_out, nand_3_out);
  Transistor #(.\type ("n"), .gate("br")) transistor_45 (.in(1'b0), .out(transistor_45_out), .gate(in_4));
  Pull_Resistor #(.pull(1)) pull_resistor_25 (.node(transistor_45_out));
  Pull_Resistor #(.pull(1)) pull_resistor_26 (.node(pull_resistor_24_node));
  Transistor #(.\type ("n")) transistor_46 (.in(transistor_43_out), .out(pull_resistor_24_node), .gate(out_11));
  nand nand_4 (nand_4_out, nand_3_out, CLK);
  nand nand_5 (Q_2, nand_4_out, QN_2);
  nand nand_6 (QN_2, Q_2, nand_7_out);
  nand nand_7 (nand_7_out, not_2_out, CLK);
  Transistor #(.\type ("n")) transistor_47 (.in(transistor_48_out), .out(out_11), .gate(pull_resistor_24_node));
  Transistor #(.\type ("n")) transistor_48 (.in(1'b0), .out(transistor_48_out), .gate(pull_resistor_24_node));
  Pull_Resistor #(.pull(1)) pull_resistor_27 (.node(out_11));
  Clock clock_3 (.out(clock_3_out));
endmodule

module _2X4_Decoder (
  input  A0,
  input  A1,
  output D0,
  output D1,
  output D2,
  output D3
);

  wire pull_resistor_1_node, transistor_2_out, transistor_3_out, transistor_5_out, transistor_7_out,
       transistor_9_out;

  Pull_Resistor #(.pull(1)) pull_resistor_1 (.node(pull_resistor_1_node));
  Transistor #(.\type ("n")) transistor_1 (.in(1'b0), .out(pull_resistor_1_node), .gate(A0));
  Transistor #(.\type ("n")) transistor_2 (.in(1'b0), .out(transistor_2_out), .gate(A1));
  Pull_Resistor #(.pull(1)) pull_resistor_2 (.node(transistor_2_out));
  Transistor #(.\type ("n")) transistor_3 (.in(1'b1), .out(transistor_3_out), .gate(pull_resistor_1_node));
  Pull_Resistor pull_resistor_3 (.node(D0));
  Transistor #(.\type ("n")) transistor_4 (.in(transistor_3_out), .out(D0), .gate(transistor_2_out));
  Transistor #(.\type ("n")) transistor_5 (.in(1'b1), .out(transistor_5_out), .gate(A0));
  Transistor #(.\type ("n")) transistor_6 (.in(transistor_5_out), .out(D1), .gate(transistor_2_out));
  Pull_Resistor pull_resistor_4 (.node(D1));
  Transistor #(.\type ("n")) transistor_7 (.in(1'b1), .out(transistor_7_out), .gate(A1));
  Pull_Resistor pull_resistor_5 (.node(D2));
  Transistor #(.\type ("n")) transistor_8 (.in(transistor_7_out), .out(D2), .gate(pull_resistor_1_node));
  Transistor #(.\type ("n")) transistor_9 (.in(1'b1), .out(transistor_9_out), .gate(A1));
  Transistor #(.\type ("n")) transistor_10 (.in(transistor_9_out), .out(D3), .gate(A0));
  Pull_Resistor pull_resistor_6 (.node(D3));
endmodule

module \and  (
  input  in_1,
  input  in_2,
  output out_3
);

  wire transistor_1_out;

  Transistor #(.\type ("n")) transistor_1 (.in(1'b1), .out(transistor_1_out), .gate(in_1));
  Transistor #(.\type ("n")) transistor_2 (.in(transistor_1_out), .out(out_3), .gate(in_2));
  Pull_Resistor pull_resistor_1 (.node(out_3));
endmodule

module main (
  input  CLK,
  input  D0,
  input  D1,
  input  W,
  input  A0,
  input  A1,
  input  S1,
  input  S0,
  input  C1,
  input  C0,
  output RD1,
  output out_12,
  output out_13,
  output out_14
);

  wire d_flip_flop_w_enable_1_q, d_flip_flop_w_enable_2_q, d_flip_flop_w_enable_3_q,
       d_flip_flop_w_enable_4_q, d_flip_flop_w_enable_5_q, d_flip_flop_w_enable_6_q,
       d_flip_flop_w_enable_7_q, d_flip_flop_w_enable_8_q, n2x1_mux_1_y, n2x1_mux_2_y, n2x1_mux_3_y,
       n2x1_mux_4_y, n2x1_mux_7_y, n2x1_mux_8_y, n2x1_mux_9_y, n2x1_mux_10_y, n2x4_decoder_1_d0,
       n2x4_decoder_1_d1, n2x4_decoder_1_d2, n2x4_decoder_1_d3, pull_resistor_3_node, pull_resistor_4_node,
       transistor_1_out, transistor_2_out, transistor_3_out, transistor_4_out, transistor_5_out,
       transistor_7_out;

  _2X4_Decoder u_2x4_decoder_1 (
    .A0(A0), .A1(A1), .D0(n2x4_decoder_1_d0), .D1(n2x4_decoder_1_d1), .D2(n2x4_decoder_1_d2),
    .D3(n2x4_decoder_1_d3));
  Transistor #(.\type ("n")) transistor_1 (.in(1'b1), .out(transistor_1_out), .gate(W));
  Transistor #(.\type ("n")) transistor_2 (.in(transistor_1_out), .out(transistor_2_out), .gate(n2x4_decoder_1_d0));
  Pull_Resistor pull_resistor_1 (.node(transistor_2_out));
  Transistor #(.\type ("n")) transistor_3 (.in(1'b1), .out(transistor_3_out), .gate(W));
  Transistor #(.\type ("n")) transistor_4 (.in(transistor_3_out), .out(transistor_4_out), .gate(n2x4_decoder_1_d1));
  Pull_Resistor pull_resistor_2 (.node(transistor_4_out));
  Transistor #(.\type ("n")) transistor_5 (.in(1'b1), .out(transistor_5_out), .gate(W));
  Pull_Resistor pull_resistor_3 (.node(pull_resistor_3_node));
  Transistor #(.\type ("n")) transistor_6 (.in(transistor_5_out), .out(pull_resistor_3_node), .gate(n2x4_decoder_1_d2));
  Transistor #(.\type ("n")) transistor_7 (.in(1'b1), .out(transistor_7_out), .gate(W));
  Pull_Resistor pull_resistor_4 (.node(pull_resistor_4_node));
  Transistor #(.\type ("n")) transistor_8 (.in(transistor_7_out), .out(pull_resistor_4_node), .gate(n2x4_decoder_1_d3));
  D_Flip_flop_w__enable d_flip_flop_w_enable_1 (
    .WD(transistor_2_out), .D(D0), .Q(d_flip_flop_w_enable_1_q), .CLK(CLK));  // open: QN
  D_Flip_flop_w__enable d_flip_flop_w_enable_2 (
    .WD(transistor_4_out), .D(D0), .Q(d_flip_flop_w_enable_2_q), .CLK(CLK));  // open: QN
  D_Flip_flop_w__enable d_flip_flop_w_enable_3 (
    .WD(pull_resistor_3_node), .D(D0), .Q(d_flip_flop_w_enable_3_q), .CLK(CLK));  // open: QN
  D_Flip_flop_w__enable d_flip_flop_w_enable_4 (
    .WD(pull_resistor_4_node), .D(D0), .Q(d_flip_flop_w_enable_4_q), .CLK(CLK));  // open: QN
  D_Flip_flop_w__enable d_flip_flop_w_enable_5 (
    .WD(transistor_2_out), .D(D1), .Q(d_flip_flop_w_enable_5_q), .CLK(CLK));  // open: QN
  D_Flip_flop_w__enable d_flip_flop_w_enable_6 (
    .WD(transistor_4_out), .D(D1), .Q(d_flip_flop_w_enable_6_q), .CLK(CLK));  // open: QN
  D_Flip_flop_w__enable d_flip_flop_w_enable_7 (
    .WD(pull_resistor_3_node), .D(D1), .Q(d_flip_flop_w_enable_7_q), .CLK(CLK));  // open: QN
  D_Flip_flop_w__enable d_flip_flop_w_enable_8 (
    .WD(pull_resistor_4_node), .D(D1), .Q(d_flip_flop_w_enable_8_q), .CLK(CLK));  // open: QN
  _2x1_Mux u_2x1_mux_1 (.A(d_flip_flop_w_enable_5_q), .B(d_flip_flop_w_enable_6_q), .Y(n2x1_mux_1_y), .S0(S0));
  _2x1_Mux u_2x1_mux_2 (.A(d_flip_flop_w_enable_7_q), .B(d_flip_flop_w_enable_8_q), .Y(n2x1_mux_2_y), .S0(S0));
  _2x1_Mux u_2x1_mux_3 (.A(d_flip_flop_w_enable_1_q), .B(d_flip_flop_w_enable_2_q), .Y(n2x1_mux_3_y), .S0(S0));
  _2x1_Mux u_2x1_mux_4 (.A(d_flip_flop_w_enable_3_q), .B(d_flip_flop_w_enable_4_q), .Y(n2x1_mux_4_y), .S0(S0));
  _2x1_Mux u_2x1_mux_5 (.A(n2x1_mux_1_y), .B(n2x1_mux_2_y), .Y(RD1), .S0(S1));
  _2x1_Mux u_2x1_mux_6 (.A(n2x1_mux_3_y), .B(n2x1_mux_4_y), .Y(out_12), .S0(S1));
  _2x1_Mux u_2x1_mux_7 (.A(d_flip_flop_w_enable_1_q), .B(d_flip_flop_w_enable_2_q), .Y(n2x1_mux_7_y), .S0(C0));
  _2x1_Mux u_2x1_mux_8 (.A(d_flip_flop_w_enable_3_q), .B(d_flip_flop_w_enable_4_q), .Y(n2x1_mux_8_y), .S0(C0));
  _2x1_Mux u_2x1_mux_9 (.A(d_flip_flop_w_enable_5_q), .B(d_flip_flop_w_enable_6_q), .Y(n2x1_mux_9_y), .S0(C0));
  _2x1_Mux u_2x1_mux_10 (.A(d_flip_flop_w_enable_7_q), .B(d_flip_flop_w_enable_8_q), .Y(n2x1_mux_10_y), .S0(C0));
  _2x1_Mux u_2x1_mux_11 (.A(n2x1_mux_7_y), .B(n2x1_mux_8_y), .Y(out_14), .S0(C1));
  _2x1_Mux u_2x1_mux_12 (.A(n2x1_mux_9_y), .B(n2x1_mux_10_y), .Y(out_13), .S0(C1));

  // Notes on the sheet:
  //   Col 0
  //   Col 1
  //   Row 0
  //   Row 1
  //   Row 2
  //   Row 3
  //   Col 0 Mux
  //   Col 1 Mux
  //   RD0
  //   Col 0 Mux
  //   Col 1 Mux
endmodule

module ALU (
  input  _01_ADDI,
  input  _10_BEQ,
  input  in_3,
  input  in_4,
  input  in_5,
  input  in_6,
  input  in_7,
  input  in_8,
  output out_9,
  output out_10,
  output out_11
);

  wire and_1_out, and_2_out, multiplexer_1_out, multiplexer_2_out, multiplexer_3_out, multiplexer_4_out,
       not_1_out, not_2_out, xor_1_out, xor_2_out, xor_4_out;

  Multiplexer #(.enable("false")) multiplexer_1 (.in0(in_6), .in1(in_8), .out(multiplexer_1_out), .sel(_10_BEQ));
  Multiplexer #(.enable("false")) multiplexer_2 (.in0(in_5), .in1(in_7), .out(multiplexer_2_out), .sel(_10_BEQ));
  Multiplexer #(.enable("false")) multiplexer_3 (
    .in0(multiplexer_1_out), .in1(xor_1_out), .out(multiplexer_3_out), .sel(_01_ADDI));
  Multiplexer #(.enable("false")) multiplexer_4 (
    .in0(multiplexer_2_out), .in1(xor_2_out), .out(multiplexer_4_out), .sel(_01_ADDI));
  not not_1 (not_1_out, multiplexer_1_out);
  not not_2 (not_2_out, multiplexer_2_out);
  xor xor_1 (xor_1_out, not_1_out, not_2_out);
  and and_1 (and_1_out, not_1_out, not_2_out);
  xor xor_2 (xor_2_out, and_1_out, 1'b1);
  xor xor_3 (out_11, in_4, multiplexer_3_out);
  and and_2 (and_2_out, in_4, multiplexer_3_out);
  xor xor_4 (xor_4_out, in_3, multiplexer_4_out);
  xor xor_5 (out_10, xor_4_out, and_2_out);
  nor nor_1 (out_9, out_11, out_10);

  // Notes on the sheet:
  //   Reg/Imm
  //   BEQ
  //   inv
  //   ADDER
  //   00 ADD
  //   11 --
endmodule
